# Fritzing sketch PerceptDK Pan and Tilt (saved by Fritzing 0.9.10b)

parts:
  Mod1 = Raspberry Pi Pico
  MPU9250_MPU-1 = SparkFun IMU Breakout - MPU-9250 [part_number=" SEN-13762"]
  PWM1 = PCA9685 16x12-bit PWM Breakout
  Pan-Servo = Basic Servo
  Tilt-Servo = Basic Servo

nets:
  N1: Mod1.pin_1, MPU9250_MPU-1.SDA/SDI, PWM1.no_name_yet#504, PWM1.no_name_yet#604
  N2: Mod1.pin_2, MPU9250_MPU-1.SCL/SCLK, PWM1.no_name_yet#503, PWM1.no_name_yet#603
  N3: Mod1.pin_8, Mod1.pin_38, MPU9250_MPU-1.GND, PWM1.no_name_yet#501, PWM1.no_name_yet#601, PWM1.no_name_yet#1000, PWM1.no_name_yet#1001
  N4: Mod1.pin_36, MPU9250_MPU-1.VDD, PWM1.no_name_yet#505, PWM1.no_name_yet#605
  N5: Mod1.pin_40, PWM1.no_name_yet#100, PWM1.no_name_yet#101, PWM1.no_name_yet#506
  N6: PWM1.no_name_yet#0, Pan-Servo.pulse
  N7: PWM1.no_name_yet#1, Tilt-Servo.pulse

custom parts:
  Raspberry Pi Pico: Raspberry Pi Pico. Based around the RP2040 microcontroller the Pico is a low cost microcontroller device bringing Raspberry Pi quality, cost, and easy of use to the microcontroller space. Jan 2021, Split part in to two versions: tht (this one) and SMD. This one will drill holes for a .1 in header in pcb to allow plugging in the module as well as providing pads to solder the module to the top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
